// Logisim project basicgates.circ as structural Verilog: 1 circuit, main circuit main
module main (
  input  in_1,
  input  in_2,
  input  in_3,
  input  in_4,
  input  in_5,
  input  in_6,
  input  in_7,
  input  in_8,
  input  in_9,
  input  in_10,
  input  in_11,
  input  in_12,
  input  in_13,
  input  in_14,
  input  in_15,
  input  in_16,
  input  in_17,
  input  in_18,
  input  in_19,
  input  in_20,
  input  in_21,
  input  in_22,
  input  in_23
);

  wire and_1_out, nand_1_out, nand_2_out, nand_3_out, nand_4_out, nand_5_out, nand_6_out, nand_7_out,
       nor_1_out, nor_2_out, nor_3_out, nor_4_out, nor_5_out, nor_6_out, nor_7_out, not_1_out, or_1_out,
       xnor_1_out, xor_1_out;

  and and_1 (and_1_out, in_1, in_5);
  nand nand_1 (nand_1_out, in_15, in_17);
  LED led_1 (.in(and_1_out));
  LED led_2 (.in(xnor_1_out));
  xnor xnor_1 (xnor_1_out, in_8, in_11);
  nor nor_1 (nor_1_out, in_19, in_19);
  nor nor_2 (nor_2_out, in_23, in_23);
  nand nand_2 (nand_2_out, nand_1_out, nand_1_out);
  LED led_3 (.in(nand_2_out));
  nor nor_3 (nor_3_out, nor_1_out, nor_2_out);
  or or_1 (or_1_out, in_2, in_6);
  LED led_4 (.in(nor_3_out));
  LED led_5 (.in(or_1_out));
  LED led_6 (.in(nand_3_out));
  nand nand_3 (nand_3_out, in_9, in_12);
  nand nand_4 (nand_4_out, in_14, in_14);
  nand nand_5 (nand_5_out, in_18, in_18);
  nor nor_4 (nor_4_out, in_20, in_22);
  not not_1 (not_1_out, in_4);
  LED led_7 (.in(not_1_out));
  nor nor_5 (nor_5_out, in_10, in_13);
  LED led_8 (.in(nand_6_out));
  nand nand_6 (nand_6_out, nand_4_out, nand_5_out);
  nor nor_6 (nor_6_out, nor_4_out, nor_4_out);
  LED led_9 (.in(nor_6_out));
  LED led_10 (.in(nor_5_out));
  xor xor_1 (xor_1_out, in_3, in_7);
  LED led_11 (.in(xor_1_out));
  nand nand_7 (nand_7_out, in_16, in_16);
  LED led_12 (.in(nand_7_out));
  nor nor_7 (nor_7_out, in_21, in_21);
  LED led_13 (.in(nor_7_out));
endmodule
